// Logisim project FF.circ as structural Verilog: 4 circuits, main circuit FFJK
module FFJK (
  input  J,
  input  Clock,
  input  K,
  input  Habilitar,
  output Q,
  output nQ
);

  wire and_1_out, and_2_out, and_3_out, buffer_1_out, not_1_out, not_2_out;

  not not_1 (not_1_out, Clock);
  buf buffer_1 (buffer_1_out, not_1_out);
  not not_2 (not_2_out, Habilitar);
  and and_1 (and_1_out, buffer_1_out, Clock);
  and and_2 (and_2_out, Q, K, and_1_out);
  and and_3 (and_3_out, and_1_out, J, nQ);
  nor nor_1 (Q, and_2_out, not_2_out, nQ);
  nor nor_2 (nQ, Q, and_3_out);
endmodule

module FFT (
  input  Clock,
  input  T,
  input  Habilitar,
  output Q,
  output nQ
);

  FFJK ffjk_1 (.J(T), .Clock(Clock), .K(T), .Habilitar(Habilitar), .Q(Q), .nQ(nQ));
endmodule

module FFSR (
  input  S,
  input  Clock,
  input  R,
  input  Habilitar,
  output Q,
  output nQ
);

  wire and_1_out, and_2_out, and_3_out, buffer_1_out, not_1_out, not_2_out;

  buf buffer_1 (buffer_1_out, not_1_out);
  not not_1 (not_1_out, Clock);
  not not_2 (not_2_out, Habilitar);
  and and_1 (and_1_out, buffer_1_out, Clock);
  and and_2 (and_2_out, R, and_1_out);
  and and_3 (and_3_out, and_1_out, S);
  nor nor_1 (Q, and_2_out, not_2_out, nQ);
  nor nor_2 (nQ, Q, and_3_out);
endmodule

module FFD (
  input  Clock,
  input  D,
  input  Habilitar,
  output Q,
  output nQ
);

  wire not_1_out;

  not not_1 (not_1_out, D);
  FFJK ffjk_1 (.J(D), .Clock(Clock), .K(not_1_out), .Habilitar(Habilitar), .Q(Q), .nQ(nQ));
endmodule
