// Logisim project Case_1.circ as structural Verilog: 1 circuit, main circuit main
module main (
  input  [11:0] Dividendo,
  input  [11:0] Divisor,
  input  [5:0] Cociente,
  input  Habilitador,
  output [11:0] out_5,
  output [11:0] out_6,
  output [5:0] out_7
);

  wire not_1_out, not_2_out, not_3_out;
  wire [11:0] main_1_out_3;

  assign out_5 = Habilitador ? Dividendo : 12'bz;  // Controlled_Buffer controlled_buffer_1
  SHRL_main main_1 (.in_1(Divisor), .in_2(1'b1), .out_3(main_1_out_3));
  assign out_7 = Habilitador ? Cociente : 6'bz;  // Controlled_Buffer controlled_buffer_2
  assign out_5 = not_1_out ? {12{1'b0}} : 12'bz;  // Controlled_Buffer controlled_buffer_3
  not not_1 (not_1_out, Habilitador);
  assign out_6 = Habilitador ? main_1_out_3 : 12'bz;  // Controlled_Buffer controlled_buffer_4
  assign out_6 = not_2_out ? {12{1'b0}} : 12'bz;  // Controlled_Buffer controlled_buffer_5
  not not_2 (not_2_out, Habilitador);
  assign out_7 = not_3_out ? {6{1'b0}} : 6'bz;  // Controlled_Buffer controlled_buffer_6
  not not_3 (not_3_out, Habilitador);
endmodule
