// Logisim project Case_2.circ as structural Verilog: 1 circuit, main circuit main
module main (
  input  [11:0] R,
  input  [11:0] D,
  input  [5:0] C,
  input  in_4,
  output [11:0] R_2,
  output [11:0] D_2,
  output [5:0] C_2
);

  wire and_1_out, main_1_sf, main_1_zf, not_1_out, not_2_out;
  wire [5:0] main_3_out_3;
  wire [11:0] main_2_out_6;

  Comp_princ_main main_1 (.A(R[5:0]), .in_2(D[11:6]), .Habilitador(1'b1), .ZF(main_1_zf), .SF(main_1_sf));
  assign R_2 = in_4 ? {{6{1'b0}}, R[5:0]} : 12'bz;  // Controlled_Buffer controlled_buffer_1
  not not_1 (not_1_out, in_4);
  assign R_2 = not_1_out ? {12{1'b0}} : 12'bz;  // Controlled_Buffer controlled_buffer_2
  Case_1_main main_2 (
    .Dividendo({D[5:0], R[5:0]}), .Divisor(D), .Cociente(C), .Habilitador(1'b1), .out_6(main_2_out_6));  // open: out_5, out_7
  assign D_2 = in_4 ? main_2_out_6 : 12'bz;  // Controlled_Buffer controlled_buffer_3
  and and_1 (and_1_out, ~main_1_zf, main_1_sf);  // AND_Gate
  assign D_2 = not_1_out ? {12{1'b0}} : 12'bz;  // Controlled_Buffer controlled_buffer_4
  assign C_2 = in_4 ? main_3_out_3 : 6'bz;  // Controlled_Buffer controlled_buffer_5
  SHL_0_main main_3 (.in_1(C), .in_2(and_1_out), .out_3(main_3_out_3));
  assign C_2 = not_2_out ? {6{1'b0}} : 6'bz;  // Controlled_Buffer controlled_buffer_6
  not not_2 (not_2_out, in_4);

  assign R[11:6] = D[5:0];
endmodule
