// Logisim project Case_3.circ as structural Verilog: 1 circuit, main circuit main
module main (
  input  [11:0] R,
  input  [11:0] D,
  input  [5:0] C,
  input  Habilitador,
  output [11:0] R_2,
  output [11:0] D_2,
  output [5:0] Cociente
);

  wire and_1_out, and_2_out, main_1_out_2, main_2_sf, main_2_zf, not_1_out, not_2_out, not_3_out, not_4_out;
  wire [5:0] main_3_resultado, main_5_out_3;
  wire [11:0] main_4_out_6;

  ZF_12_main main_1 (.in_1(R), .out_2(main_1_out_2));
  not not_1 (not_1_out, main_1_out_2);
  Comp_princ_main main_2 (.A(R[5:0]), .in_2(D[5:0]), .Habilitador(1'b1), .ZF(main_2_zf), .SF(main_2_sf));
  and and_1 (and_1_out, not_1_out, and_2_out);
  and and_2 (and_2_out, ~main_2_zf, ~main_2_sf);  // AND_Gate
  Sum_rest_6bits_main main_3 (
    .A(R[5:0]), .B(D[5:0]), .Carry(1'b0), .Habilitador(and_1_out), .Suma_0___Resta_1(1'b1),
    .Resultado(main_3_resultado));  // open: CF, SF, ZF
  assign R_2 = not_2_out ? {12{1'b0}} : 12'bz;  // Controlled_Buffer controlled_buffer_1
  not not_2 (not_2_out, Habilitador);
  Case_1_main main_4 (
    .Dividendo(R), .Divisor(D), .Cociente(C), .Habilitador(1'b1), .out_6(main_4_out_6));  // open: out_5, out_7
  SHL_1_main main_5 (.in_1(C), .in_2(1'b1), .out_3(main_5_out_3));
  assign D_2 = Habilitador ? main_4_out_6 : 12'bz;  // Controlled_Buffer controlled_buffer_2
  assign D_2 = not_3_out ? {12{1'b0}} : 12'bz;  // Controlled_Buffer controlled_buffer_3
  not not_3 (not_3_out, Habilitador);
  assign Cociente = Habilitador ? main_5_out_3 : 6'bz;  // Controlled_Buffer controlled_buffer_4
  assign Cociente = not_4_out ? {6{1'b0}} : 6'bz;  // Controlled_Buffer controlled_buffer_5
  not not_4 (not_4_out, Habilitador);
  assign R_2 = Habilitador ? {{6{1'b0}}, main_3_resultado} : 12'bz;  // Controlled_Buffer controlled_buffer_6
endmodule
