// Logisim project Clasificador.circ as structural Verilog: 1 circuit, main circuit main
module main (
  input  [11:0] R,
  input  [11:0] D,
  output [1:0] out_3
);

  wire and_1_out, and_2_out, and_3_out, and_4_out, main_1_sf, main_1_zf, main_2_out_2, not_1_out, or_1_out;

  Comp_princ_main main_1 (.A(R[5:0]), .in_2(D[11:6]), .Habilitador(1'b1), .ZF(main_1_zf), .SF(main_1_sf));
  not not_1 (not_1_out, main_2_out_2);
  and and_1 (and_1_out, ~main_1_zf, main_1_sf);  // AND_Gate
  and and_2 (and_2_out, ~main_1_zf, ~main_1_sf);  // AND_Gate
  and and_3 (and_3_out, main_1_zf, ~main_1_sf);  // AND_Gate
  ZF_12_main main_2 (.in_1(D), .out_2(main_2_out_2));
  or or_1 (or_1_out, and_2_out, and_3_out);
  and and_4 (and_4_out, or_1_out, not_1_out);
  or or_2 (out_3[1], and_1_out, and_4_out);
  or or_3 (out_3[0], and_4_out, main_2_out_2);

  assign R[11:6] = D[5:0];

  // Notes on the sheet:
  //   2
  //   1
  //   3
endmodule
