// Logisim project Comp_princ.circ as structural Verilog: 1 circuit, main circuit main
module main (
  input  [5:0] A,
  input  [5:0] in_2,
  input  Habilitador,
  output ZF,
  output SF
);

  // Comparador_main main_1: pin names not known; wires that end beside it: A, in_2, Habilitador, ZF, SF

  // Notes on the sheet:
  //   B
endmodule
