// Logisim project Comparador.circ as structural Verilog: 1 circuit, main circuit main
module main (
  input  [5:0] A,
  input  [5:0] B,
  input  in_3,
  output ZF,
  output SF
);

  wire and_1_out, main_1_resultado, main_2_resultado, main_3_resultado, main_4_resultado, main_5_resultado,
       main_6_resultado;

  Comparador1_main main_1 (.A(A[0]), .B(B[0]), .Resultado(main_1_resultado));
  Comparador1_main main_2 (.A(A[1]), .B(B[1]), .Resultado(main_2_resultado));
  Comparador1_main main_3 (.A(A[2]), .B(B[2]), .Resultado(main_3_resultado));
  Comparador1_main main_4 (.A(A[3]), .B(B[3]), .Resultado(main_4_resultado));
  Comparador1_main main_5 (.A(A[4]), .B(B[4]), .Resultado(main_5_resultado));
  Comparador1_main main_6 (.A(A[5]), .B(B[5]), .Resultado(main_6_resultado));
  Comparador3_main main_7 (.B(B), .A(A), .Habilitador(in_3), .Cuando_A_B(SF));
  and and_1 (and_1_out, main_1_resultado, main_2_resultado, main_3_resultado, main_4_resultado, main_5_resultado, main_6_resultado);
  and and_2 (ZF, and_1_out, in_3);
endmodule
