// Logisim project Comparador2.circ as structural Verilog: 1 circuit, main circuit main
module main (
  input  A,
  input  B,
  output Resultado
);

  wire not_1_out;

  not not_1 (not_1_out, B);
  and and_1 (Resultado, A, not_1_out);
endmodule
