// Logisim project Comparador3.circ as structural Verilog: 1 circuit, main circuit main
module main (
  input  [5:0] B,
  input  [5:0] A,
  input  Habilitador,
  output Cuando_A_B
);

  wire and_1_out, and_2_out, and_3_out, and_4_out, and_5_out, and_6_out, and_7_out, main_1_resultado,
       main_2_resultado, main_3_resultado, main_4_resultado, main_5_resultado, main_6_resultado,
       main_7_resultado, main_8_resultado, main_9_resultado, main_10_resultado, main_11_resultado,
       main_12_resultado, main_13_resultado, main_14_resultado, main_15_resultado, main_16_resultado,
       main_17_resultado, main_18_resultado, main_19_resultado, main_20_resultado, main_21_resultado,
       or_1_out, or_2_out, or_3_out, or_4_out, or_5_out;

  Comparador2_main main_1 (.A(B[0]), .B(A[0]), .Resultado(main_1_resultado));
  Comparador1_main main_2 (.A(B[1]), .B(A[1]), .Resultado(main_2_resultado));
  Comparador1_main main_3 (.A(B[2]), .B(A[2]), .Resultado(main_3_resultado));
  Comparador2_main main_4 (.A(B[1]), .B(A[1]), .Resultado(main_4_resultado));
  Comparador1_main main_5 (.A(B[2]), .B(A[2]), .Resultado(main_5_resultado));
  Comparador1_main main_6 (.A(B[3]), .B(A[3]), .Resultado(main_6_resultado));
  Comparador1_main main_7 (.A(B[4]), .B(A[4]), .Resultado(main_7_resultado));
  Comparador1_main main_8 (.A(B[5]), .B(A[5]), .Resultado(main_8_resultado));
  Comparador2_main main_9 (.A(B[5]), .B(A[5]), .Resultado(main_9_resultado));
  Comparador1_main main_10 (.A(B[3]), .B(A[3]), .Resultado(main_10_resultado));
  Comparador1_main main_11 (.A(B[4]), .B(A[4]), .Resultado(main_11_resultado));
  Comparador1_main main_12 (.A(B[5]), .B(A[5]), .Resultado(main_12_resultado));
  Comparador2_main main_13 (.A(B[2]), .B(A[2]), .Resultado(main_13_resultado));
  Comparador1_main main_14 (.A(B[3]), .B(A[3]), .Resultado(main_14_resultado));
  Comparador1_main main_15 (.A(B[4]), .B(A[4]), .Resultado(main_15_resultado));
  Comparador1_main main_16 (.A(B[5]), .B(A[5]), .Resultado(main_16_resultado));
  Comparador2_main main_17 (.A(B[3]), .B(A[3]), .Resultado(main_17_resultado));
  Comparador1_main main_18 (.A(B[4]), .B(A[4]), .Resultado(main_18_resultado));
  Comparador1_main main_19 (.A(B[5]), .B(A[5]), .Resultado(main_19_resultado));
  Comparador2_main main_20 (.A(B[4]), .B(A[4]), .Resultado(main_20_resultado));
  Comparador1_main main_21 (.A(B[5]), .B(A[5]), .Resultado(main_21_resultado));
  and and_1 (and_1_out, main_1_resultado, main_2_resultado, main_3_resultado);
  and and_2 (and_2_out, main_4_resultado, main_5_resultado, main_6_resultado, main_7_resultado, main_8_resultado);
  and and_3 (and_3_out, main_10_resultado, main_11_resultado, main_12_resultado);
  and and_4 (and_4_out, main_13_resultado, main_14_resultado, main_15_resultado, main_16_resultado);
  and and_5 (and_5_out, main_17_resultado, main_18_resultado, main_19_resultado);
  and and_6 (and_6_out, main_20_resultado, main_21_resultado);
  and and_7 (and_7_out, and_1_out, and_3_out);
  or or_1 (or_1_out, main_9_resultado, and_6_out);
  or or_2 (or_2_out, and_4_out, and_5_out);
  or or_3 (or_3_out, and_7_out, and_2_out);
  or or_4 (or_4_out, or_1_out, or_2_out);
  or or_5 (or_5_out, or_3_out, or_4_out);
  and and_8 (Cuando_A_B, or_5_out, Habilitador);
endmodule
