// Logisim project Compl2-6bits.circ as structural Verilog: 1 circuit, main circuit main
module main (
  input  [5:0] Palabra,
  input  carry_in,
  input  Habilitador,
  output carry_out,
  output [5:0] Resultado
);

  wire main_1_out_2, main_2_out_2;
  wire [0:0] not_1_out;
  wire [5:0] not_2_out, select_6_1_respuesta;

  ZF_6_main main_1 (.in_1(Palabra), .out_2(main_1_out_2));
  not not_1 (not_1_out[0], main_1_out_2);
  not not_2 (not_2_out[0], Palabra[0]);
  not not_3 (not_2_out[1], Palabra[1]);
  not not_4 (not_2_out[2], Palabra[2]);
  not not_5 (not_2_out[3], Palabra[3]);
  not not_6 (not_2_out[4], Palabra[4]);
  not not_7 (not_2_out[5], Palabra[5]);
  ZF_6_main main_2 (.in_1(Palabra), .out_2(main_2_out_2));
  Select_6 select_6_1 (.A(not_2_out), .B({6{1'b0}}), .Habilitador(main_2_out_2), .Respuesta(select_6_1_respuesta));
  Sumador_6bits sumador_6bits_1 (
    .in_1({{5{1'b0}}, not_1_out[0]}), .in_2(select_6_1_respuesta), .Carry(carry_in),
    .Habilitador(Habilitador), .carry_out(carry_out), .bit5(Resultado[5]), .bit_4(Resultado[4]),
    .bit_3(Resultado[3]), .bit_2(Resultado[2]), .bit_1(Resultado[1]), .bit_0(Resultado[0]));

  // Notes on the sheet:
  //   seleccionador
endmodule
