// Logisim project Divisor.circ as structural Verilog: 1 circuit, main circuit main
module main (
  input  [5:0] Dividendo,
  input  [5:0] Divisor,
  input  Habilitador,
  output [5:0] Residuo,
  output [5:0] Cociente,
  output ZF,
  output SF
);

  wire and_1_out, and_2_out, and_3_out, main_2_signo, main_3_signo, main_5_signo, main_6_signo, main_7_sf,
       main_7_zf, main_9_out_2, main_15_out_2, not_1_out, or_1_out, xor_1_out;
  wire [5:0] controlled_buffer_1_out, controlled_buffer_2_out, main_1_resultado, main_4_resultado,
       main_8_cociente_2, main_10_cociente_2, main_11_cociente_2, main_12_resultado, main_13_cociente_2,
       main_14_cociente_2, main_17_cociente_2, main_18_cociente_2, main_18_residuo, select_6_1_respuesta,
       select_6_2_respuesta, select_6_3_respuesta;
  wire [11:0] main_8_divisor_2, main_8_residuo, main_10_divisor_2, main_10_residuo, main_11_divisor_2,
       main_11_residuo, main_13_divisor_2, main_13_residuo, main_14_divisor_2, main_14_residuo,
       main_17_divisor_2, main_17_residuo;
  wire [11:6] main_18_residuo_2;

  Compl2_6bits_main main_1 (
    .Palabra(Dividendo), .carry_in(1'b0), .Habilitador(1'b1), .Resultado(main_1_resultado));  // open: carry_out
  SF_6_main main_2 (.Palabra(Dividendo), .Signo(main_2_signo));
  SF_6_main main_3 (.Palabra(Divisor), .Signo(main_3_signo));
  Compl2_6bits_main main_4 (
    .Palabra(Divisor), .carry_in(1'b0), .Habilitador(1'b1), .Resultado(main_4_resultado));  // open: carry_out
  Select_6 select_6_1 (
    .A(Dividendo), .B(main_1_resultado), .Habilitador(main_2_signo), .Respuesta(select_6_1_respuesta));
  Select_6 select_6_2 (.A(Divisor), .B(main_4_resultado), .Habilitador(main_3_signo), .Respuesta(select_6_2_respuesta));
  SF_6_main main_5 (.Palabra(Dividendo), .Signo(main_5_signo));
  SF_6_main main_6 (.Palabra(Divisor), .Signo(main_6_signo));
  Comp_princ_main main_7 (.A(Dividendo), .in_2(Divisor), .Habilitador(Habilitador), .ZF(main_7_zf), .SF(main_7_sf));
  and and_1 (and_1_out, ~main_5_signo, Habilitador, ~main_6_signo);  // AND_Gate
  and and_2 (and_2_out, ~main_7_zf, main_7_sf);  // AND_Gate
  and and_3 (and_3_out, and_2_out, and_1_out);
  Multiplexor_main main_8 (
    .Dividendo({{6{1'b0}}, select_6_1_respuesta}), .Divisor({select_6_2_respuesta, {6{1'b0}}}),
    .Cociente({6{1'b0}}), .Residuo(main_8_residuo), .Divisor_2(main_8_divisor_2),
    .Cociente_2(main_8_cociente_2));
  assign controlled_buffer_1_out = Habilitador ? main_18_residuo : 6'bz;  // Controlled_Buffer controlled_buffer_1
  assign controlled_buffer_2_out = Habilitador ? main_18_cociente_2 : 6'bz;  // Controlled_Buffer controlled_buffer_2
  assign controlled_buffer_1_out = not_1_out ? {6{1'b0}} : 6'bz;  // Controlled_Buffer controlled_buffer_3
  not not_1 (not_1_out, Habilitador);
  xor xor_1 (xor_1_out, main_2_signo, main_3_signo);
  ZF_6_main main_9 (.in_1(Dividendo), .out_2(main_9_out_2));
  Multiplexor_main main_10 (
    .Dividendo(main_8_residuo), .Divisor(main_8_divisor_2), .Cociente(main_8_cociente_2),
    .Residuo(main_10_residuo), .Divisor_2(main_10_divisor_2), .Cociente_2(main_10_cociente_2));
  assign controlled_buffer_2_out = not_1_out ? {6{1'b0}} : 6'bz;  // Controlled_Buffer controlled_buffer_4
  Multiplexor_main main_11 (
    .Dividendo(main_10_residuo), .Divisor(main_10_divisor_2), .Cociente(main_10_cociente_2),
    .Residuo(main_11_residuo), .Divisor_2(main_11_divisor_2), .Cociente_2(main_11_cociente_2));
  Compl2_6bits_main main_12 (
    .Palabra(controlled_buffer_2_out), .carry_in(1'b0), .Habilitador(1'b1), .Resultado(main_12_resultado));  // open: carry_out
  assign ZF = Habilitador ? or_1_out : 1'bz;  // Controlled_Buffer controlled_buffer_5
  or or_1 (or_1_out, main_15_out_2, main_9_out_2);
  assign ZF = not_1_out ? 1'b0 : 1'bz;  // Controlled_Buffer controlled_buffer_6
  Multiplexor_main main_13 (
    .Dividendo(main_11_residuo), .Divisor(main_11_divisor_2), .Cociente(main_11_cociente_2),
    .Residuo(main_13_residuo), .Divisor_2(main_13_divisor_2), .Cociente_2(main_13_cociente_2));
  Select_6 select_6_3 (
    .A(controlled_buffer_2_out), .B(main_12_resultado), .Habilitador(xor_1_out),
    .Respuesta(select_6_3_respuesta));
  Select_6 select_6_4 (.A(controlled_buffer_1_out), .B(Dividendo), .Habilitador(and_3_out), .Respuesta(Residuo));
  Select_6 select_6_5 (.A(select_6_3_respuesta), .B({6{1'b0}}), .Habilitador(and_3_out), .Respuesta(Cociente));
  Multiplexor_main main_14 (
    .Dividendo(main_13_residuo), .Divisor(main_13_divisor_2), .Cociente(main_13_cociente_2),
    .Residuo(main_14_residuo), .Divisor_2(main_14_divisor_2), .Cociente_2(main_14_cociente_2));
  // Probe on Residuo
  // Probe on select_6_3_respuesta
  ZF_6_main main_15 (.in_1(select_6_2_respuesta), .out_2(main_15_out_2));
  SF_6_main main_16 (.Palabra(select_6_3_respuesta), .Signo(SF));
  Multiplexor_main main_17 (
    .Dividendo(main_14_residuo), .Divisor(main_14_divisor_2), .Cociente(main_14_cociente_2),
    .Residuo(main_17_residuo), .Divisor_2(main_17_divisor_2), .Cociente_2(main_17_cociente_2));
  Multiplexor_main main_18 (
    .Dividendo(main_17_residuo), .Divisor(main_17_divisor_2), .Cociente(main_17_cociente_2),
    .Residuo({main_18_residuo_2, main_18_residuo}), .Cociente_2(main_18_cociente_2));  // open: Divisor_2

  // Notes on the sheet:
  //   cantidad de multiplexores = n + 1
endmodule
