// Logisim project Multiplexor.circ as structural Verilog: 1 circuit, main circuit main
module main (
  input  [11:0] Dividendo,
  input  [11:0] Divisor,
  input  [5:0] Cociente,
  output [11:0] Residuo,
  output [11:0] Divisor_2,
  output [5:0] Cociente_2
);

  wire and_1_out, and_2_out, and_3_out;
  wire [1:0] main_1_out_3;
  wire [5:0] main_2_out_7, main_3_c_2, main_4_cociente;
  wire [11:0] main_2_out_5, main_2_out_6, main_3_d_2, main_3_r_2, main_4_d_2, main_4_r_2;

  Clasificador_main main_1 (.R(Dividendo), .D(Divisor), .out_3(main_1_out_3));
  and and_1 (and_1_out, main_1_out_3[0], ~main_1_out_3[1]);  // AND_Gate
  and and_2 (and_2_out, ~main_1_out_3[0], main_1_out_3[1]);  // AND_Gate
  and and_3 (and_3_out, main_1_out_3[0], main_1_out_3[1]);
  Case_1_main main_2 (
    .Dividendo(Dividendo), .Divisor(Divisor), .Cociente(Cociente), .Habilitador(and_1_out),
    .out_5(main_2_out_5), .out_6(main_2_out_6), .out_7(main_2_out_7));
  Case_2_main main_3 (
    .R(Dividendo), .D(Divisor), .C(Cociente), .in_4(and_2_out), .R_2(main_3_r_2), .D_2(main_3_d_2),
    .C_2(main_3_c_2));
  Case_3_main main_4 (
    .R(Dividendo), .D(Divisor), .C(Cociente), .Habilitador(and_3_out), .R_2(main_4_r_2), .D_2(main_4_d_2),
    .Cociente(main_4_cociente));
  assign Residuo = main_2_out_5 | main_3_r_2 | main_4_r_2;  // OR_Gate or_1, 12 bits wide
  assign Divisor_2 = main_2_out_6 | main_3_d_2 | main_4_d_2;  // OR_Gate or_2, 12 bits wide
  assign Cociente_2 = main_2_out_7 | main_3_c_2 | main_4_cociente;  // OR_Gate or_3, 6 bits wide
endmodule
