// Logisim project SHL_1.circ as structural Verilog: 1 circuit, main circuit main
module main (
  input  [5:0] in_1,
  input  in_2,
  output [5:0] out_3
);

  and and_1 (out_3[1], in_1[0], in_2);
  and and_2 (out_3[2], in_1[1], in_2);
  and and_3 (out_3[3], in_1[2], in_2);
  and and_4 (out_3[4], in_1[3], in_2);
  and and_5 (out_3[5], in_1[4], in_2);

  assign out_3[0] = 1'b1;
endmodule
