// Logisim project SHRL.circ as structural Verilog: 1 circuit, main circuit main
module main (
  input  [11:0] in_1,
  input  in_2,
  output [11:0] out_3
);

  and and_1 (out_3[0], in_2, in_1[1]);
  and and_2 (out_3[1], in_2, in_1[2]);
  and and_3 (out_3[2], in_2, in_1[3]);
  and and_4 (out_3[3], in_2, in_1[4]);
  and and_5 (out_3[4], in_2, in_1[5]);
  and and_6 (out_3[5], in_2, in_1[6]);
  and and_7 (out_3[6], in_2, in_1[7]);
  and and_8 (out_3[7], in_2, in_1[8]);
  and and_9 (out_3[8], in_2, in_1[9]);
  and and_10 (out_3[9], in_2, in_1[10]);
  and and_11 (out_3[10], in_2, in_1[11]);

  assign out_3[11] = 1'b0;
endmodule
