// Logisim project Select-1.circ as structural Verilog: 1 circuit, main circuit Select-1
module Select_1 (
  input  A,
  input  B,
  input  Control,
  output Respuesta
);

  wire and_1_out, and_2_out, not_1_out;

  not not_1 (not_1_out, Control);
  and and_1 (and_1_out, A, not_1_out);
  and and_2 (and_2_out, B, Control);
  or or_1 (Respuesta, and_1_out, and_2_out);
endmodule
