// Logisim project Select-6.circ as structural Verilog: 1 circuit, main circuit Select-6
module Select_6 (
  input  [5:0] A,
  input  [5:0] B,
  input  Habilitador,
  output [5:0] Respuesta
);

  Select_1 select_1_1 (.A(A[0]), .B(B[0]), .Control(Habilitador), .Respuesta(Respuesta[0]));
  Select_1 select_1_2 (.A(A[1]), .B(B[1]), .Control(Habilitador), .Respuesta(Respuesta[1]));
  Select_1 select_1_3 (.A(A[2]), .B(B[2]), .Control(Habilitador), .Respuesta(Respuesta[2]));
  Select_1 select_1_4 (.A(A[3]), .B(B[3]), .Control(Habilitador), .Respuesta(Respuesta[3]));
  Select_1 select_1_5 (.A(A[4]), .B(B[4]), .Control(Habilitador), .Respuesta(Respuesta[4]));
  Select_1 select_1_6 (.A(A[5]), .B(B[5]), .Control(Habilitador), .Respuesta(Respuesta[5]));

  // Notes on the sheet:
  //   Permite es coger entre que palabra dejar pasar, con 0 para A, con 1 pasa B
endmodule
