// Logisim project Sum-rest_6bits.circ as structural Verilog: 1 circuit, main circuit main
module main (
  input  [5:0] A,
  input  [5:0] B,
  input  Carry,
  input  Habilitador,
  input  Suma_0___Resta_1,
  output CF,
  output [5:0] Resultado,
  output SF,
  output ZF
);

  wire main_1_carry_out, main_2_signo, main_3_out_2;
  wire [5:0] main_1_resultado, select_6_1_respuesta;

  Compl2_6bits_main main_1 (
    .Palabra(B), .carry_in(1'b0), .Habilitador(1'b1), .carry_out(main_1_carry_out),
    .Resultado(main_1_resultado));
  Select_6 select_6_1 (.A(B), .B(main_1_resultado), .Habilitador(Suma_0___Resta_1), .Respuesta(select_6_1_respuesta));
  Sumador_6bits sumador_6bits_1 (
    .in_1(A), .in_2(select_6_1_respuesta), .Carry(Carry), .Habilitador(Habilitador), .carry_out(CF),
    .bit5(Resultado[5]), .bit_4(Resultado[4]), .bit_3(Resultado[3]), .bit_2(Resultado[2]),
    .bit_1(Resultado[1]), .bit_0(Resultado[0]));
  SF_6_main main_2 (.Palabra(Resultado), .Signo(main_2_signo));
  ZF_6_main main_3 (.in_1(Resultado), .out_2(main_3_out_2));
  and and_1 (SF, Habilitador, main_2_signo);
  and and_2 (ZF, main_3_out_2, Habilitador);
  // also tied to GND on the sheet: main_1_carry_out
endmodule
