// Logisim project Sum_1bit.circ as structural Verilog: 1 circuit, main circuit Sum_1bit
module Sum_1bit (
  input  A,
  input  B,
  input  Carry_in,
  output Resultado,
  output Carry_out
);

  wire and_1_out, and_2_out, xor_1_out;

  xor xor_1 (xor_1_out, A, B);
  and and_1 (and_1_out, B, A);
  and and_2 (and_2_out, Carry_in, xor_1_out);
  xor xor_2 (Resultado, xor_1_out, Carry_in);
  or or_1 (Carry_out, and_1_out, and_2_out);
endmodule
