// Logisim project Test.circ as structural Verilog: 1 circuit, main circuit main
module main (
  input  [5:0] Dividendo,
  input  [5:0] Divisor,
  input  in_3,
  output [5:0] Residuo,
  output [5:0] Cociente,
  output ZF,
  output SF
);

  Divisor_main main_1 (
    .Dividendo(Dividendo), .Divisor(Divisor), .Habilitador(in_3), .Residuo(Residuo), .Cociente(Cociente),
    .ZF(ZF), .SF(SF));
endmodule
