// Logisim project ZF-12.circ as structural Verilog: 1 circuit, main circuit main
module main (
  input  [11:0] in_1,
  output out_2
);

  and and_1 (out_2, ~in_1[0], ~in_1[1], ~in_1[2], ~in_1[3], ~in_1[4], ~in_1[5]);  // AND_Gate
endmodule
