// Logisim project sumador_6bits.circ as structural Verilog: 1 circuit, main circuit Sumador_6bits
module Sumador_6bits (
  input  [5:0] in_1,
  input  [5:0] in_2,
  input  Carry,
  input  Habilitador,
  output carry_out,
  output bit5,
  output bit_4,
  output bit_3,
  output bit_2,
  output bit_1,
  output bit_0
);

  wire sum_1bit_1_carry_out, sum_1bit_1_resultado, sum_1bit_2_carry_out, sum_1bit_2_resultado,
       sum_1bit_3_carry_out, sum_1bit_3_resultado, sum_1bit_4_carry_out, sum_1bit_4_resultado,
       sum_1bit_5_carry_out, sum_1bit_5_resultado, sum_1bit_6_carry_out, sum_1bit_6_resultado;

  and and_1 (bit5, sum_1bit_6_resultado, Habilitador);
  Sum_1bit sum_1bit_1 (
    .A(in_1[0]), .B(in_2[0]), .Carry_in(Carry), .Resultado(sum_1bit_1_resultado),
    .Carry_out(sum_1bit_1_carry_out));
  and and_2 (bit_4, sum_1bit_5_resultado, Habilitador);
  Sum_1bit sum_1bit_2 (
    .A(in_1[1]), .B(in_2[1]), .Carry_in(sum_1bit_1_carry_out), .Resultado(sum_1bit_2_resultado),
    .Carry_out(sum_1bit_2_carry_out));
  and and_3 (bit_3, sum_1bit_4_resultado, Habilitador);
  and and_4 (bit_2, sum_1bit_3_resultado, Habilitador);
  Sum_1bit sum_1bit_3 (
    .A(in_1[2]), .B(in_2[2]), .Carry_in(sum_1bit_2_carry_out), .Resultado(sum_1bit_3_resultado),
    .Carry_out(sum_1bit_3_carry_out));
  Sum_1bit sum_1bit_4 (
    .A(in_1[3]), .B(in_2[3]), .Carry_in(sum_1bit_3_carry_out), .Resultado(sum_1bit_4_resultado),
    .Carry_out(sum_1bit_4_carry_out));
  and and_5 (bit_1, sum_1bit_2_resultado, Habilitador);
  Sum_1bit sum_1bit_5 (
    .A(in_1[4]), .B(in_2[4]), .Carry_in(sum_1bit_4_carry_out), .Resultado(sum_1bit_5_resultado),
    .Carry_out(sum_1bit_5_carry_out));
  and and_6 (bit_0, sum_1bit_1_resultado, Habilitador);
  Sum_1bit sum_1bit_6 (
    .A(in_1[5]), .B(in_2[5]), .Carry_in(sum_1bit_5_carry_out), .Resultado(sum_1bit_6_resultado),
    .Carry_out(sum_1bit_6_carry_out));
  and and_7 (carry_out, Habilitador, sum_1bit_6_carry_out);

  // Notes on the sheet:
  //   A
  //   B
endmodule
