// Logisim project Quiz-Tarea.circ as structural Verilog: 5 circuits, main circuit Contador
module TEST (
  input  Control,
  input  Habilitador,
  output [3:0] Salida
);

  wire Auto__Clk_out;

  Clock Auto__Clk (.out(Auto__Clk_out));
  Contador contador_1 (
    .Clock(Auto__Clk_out), .Salida(Salida), .Control(Control), .Habilitador(Habilitador));  // open: Reset
  // Probe on Salida
endmodule

module Contador (
  input  Clock,
  input  Habilitador,
  input  Control,
  input  Reset,
  output [3:0] Salida
);

  wire and_1_out, n4_bit_ff_d_paridad_1_paridad, not_1_out, or_1_out;
  wire [3:0] calcular_suma_1_salida, n4_bit_sumador_1_out_3;

  not not_1 (not_1_out, Reset);
  and and_1 (and_1_out, Clock, Habilitador);
  _4_bit_FF_D___Paridad u_4_bit_ff_d_paridad_1 (
    .Clock(and_1_out), .Entrada(n4_bit_sumador_1_out_3), .Reset(or_1_out), .Salida(Salida),
    .Paridad(n4_bit_ff_d_paridad_1_paridad));
  or or_1 (or_1_out, Habilitador, not_1_out);
  Calcular_suma calcular_suma_1 (
    .Ctrl(Control), .Paridad(n4_bit_ff_d_paridad_1_paridad), .Salida(calcular_suma_1_salida));
  _4_bit_Sumador u_4_bit_sumador_1 (.in_1(Salida), .in_2(calcular_suma_1_salida), .out_3(n4_bit_sumador_1_out_3));
endmodule

module _4_bit_FF_D___Paridad (
  input  Clock,
  input  [3:0] Entrada,
  input  Reset,
  output [3:0] Salida,
  output Paridad
);

  FFD ffd_1 (.Clock(Clock), .D(Entrada[0]), .Habilitar(Reset), .Q(Paridad));  // open: nQ
  FFD ffd_2 (.Clock(Clock), .D(Entrada[1]), .Habilitar(Reset), .Q(Salida[1]));  // open: nQ
  FFD ffd_3 (.Clock(Clock), .D(Entrada[2]), .Habilitar(Reset), .Q(Salida[2]));  // open: nQ
  FFD ffd_4 (.Clock(Clock), .D(Entrada[3]), .Habilitar(Reset), .Q(Salida[3]));  // open: nQ

  assign Salida[0] = Paridad;
endmodule

module _4_bit_Sumador (
  input  [3:0] in_1,
  input  [3:0] in_2,
  output [3:0] out_3
);

  wire sum_1bit_1_carry_out, sum_1bit_2_carry_out, sum_1bit_3_carry_out;

  Sum_1bit sum_1bit_1 (
    .A(in_1[1]), .B(in_2[1]), .Carry_in(sum_1bit_2_carry_out), .Resultado(out_3[1]),
    .Carry_out(sum_1bit_1_carry_out));
  Sum_1bit sum_1bit_2 (
    .A(in_1[0]), .B(in_2[0]), .Carry_in(1'b0), .Resultado(out_3[0]), .Carry_out(sum_1bit_2_carry_out));
  Sum_1bit sum_1bit_3 (
    .A(in_1[2]), .B(in_2[2]), .Carry_in(sum_1bit_1_carry_out), .Resultado(out_3[2]),
    .Carry_out(sum_1bit_3_carry_out));
  Sum_1bit sum_1bit_4 (
    .A(in_1[3]), .B(in_2[3]), .Carry_in(sum_1bit_3_carry_out), .Resultado(out_3[3]));  // open: Carry_out
endmodule

module Calcular_suma (
  input  Ctrl,
  input  Paridad,
  output [3:0] Salida
);

  or or_1 (Salida[1], Ctrl, Paridad);
  xnor xnor_1 (Salida[0], Ctrl, Paridad);

  assign Salida[3:2] = {2{Ctrl}};
endmodule
