// Logisim project MAR.circ as structural Verilog: 2 circuits, main circuit MAR
module MAR (
  input  Clock,
  input  Reset,
  input  [3:0] Adress_In,
  input  R___W,
  input  Enable,
  output [3:0] Adress_Out
);

  _4_bit_Cell u_4_bit_cell_1 (
    .Enable(Enable), .R_W(R___W), .Data_In(Adress_In), .Data_Out(Adress_Out), .Clock(Clock), .Reset(Reset));

  // Notes on the sheet:
  //   Memory Adress Register
endmodule

module _4_bit_Cell (
  input  Clock,
  input  Enable,
  input  R_W,
  input  [3:0] Data_In,
  input  Reset,
  output [3:0] Data_Out
);

  wire and_1_out, and_2_out, not_1_out, not_2_out;
  wire [3:0] ffd_1_q;

  and and_1 (and_1_out, Enable, ~R_W);  // AND_Gate
  and and_2 (and_2_out, Clock, Enable, R_W);
  not not_1 (not_1_out, Reset);
  FFD ffd_1 (.Clock(and_2_out), .D(Data_In[0]), .Habilitar(not_1_out), .Q(ffd_1_q[0]));  // open: nQ
  FFD ffd_2 (.Clock(and_2_out), .D(Data_In[1]), .Habilitar(not_1_out), .Q(ffd_1_q[1]));  // open: nQ
  FFD ffd_3 (.Clock(and_2_out), .D(Data_In[2]), .Habilitar(not_1_out), .Q(ffd_1_q[2]));  // open: nQ
  FFD ffd_4 (.Clock(and_2_out), .D(Data_In[3]), .Habilitar(not_1_out), .Q(ffd_1_q[3]));  // open: nQ
  not not_2 (not_2_out, and_1_out);
  assign Data_Out = and_1_out ? ffd_1_q : 4'bz;  // Controlled_Buffer controlled_buffer_1
  assign Data_Out = not_2_out ? 4'b0000 : 4'bz;  // Controlled_Buffer controlled_buffer_2
endmodule
