// Logisim project MDR.circ as structural Verilog: 2 circuits, main circuit 6 bit Cell
module MDR (
  input  Clock,
  input  Memory_Unit_R_W,
  input  Reset,
  input  [5:0] RAM_Data_In,
  input  [5:0] Bus_Data_In,
  input  MDR_R___W,
  input  Enable,
  output [5:0] RAM_Data_Out,
  output [5:0] Bus_Data_Out
);

  wire and_1_out, not_1_out, not_2_out;
  wire [5:0] controlled_buffer_1_out, n6_bit_cell_1_data_out;

  not not_1 (not_1_out, Memory_Unit_R_W);
  assign controlled_buffer_1_out = not_1_out ? RAM_Data_In : 6'bz;  // Controlled_Buffer controlled_buffer_1
  assign controlled_buffer_1_out = Memory_Unit_R_W ? Bus_Data_In : 6'bz;  // Controlled_Buffer controlled_buffer_2
  and and_1 (and_1_out, MDR_R___W, Clock);
  _6_bit_Cell u_6_bit_cell_1 (
    .Enable(Enable), .R_W(MDR_R___W), .Data_In(controlled_buffer_1_out), .Data_Out(n6_bit_cell_1_data_out),
    .Clock(and_1_out), .Reset(Reset));  // open: Reset_Out, Clock_Out
  not not_2 (not_2_out, Memory_Unit_R_W);
  assign RAM_Data_Out = Memory_Unit_R_W ? n6_bit_cell_1_data_out : 6'bz;  // Controlled_Buffer controlled_buffer_3
  assign RAM_Data_Out = not_2_out ? {6{1'b0}} : 6'bz;  // Controlled_Buffer controlled_buffer_4
  assign Bus_Data_Out = not_2_out ? n6_bit_cell_1_data_out : 6'bz;  // Controlled_Buffer controlled_buffer_5
  assign Bus_Data_Out = Memory_Unit_R_W ? {6{1'b0}} : 6'bz;  // Controlled_Buffer controlled_buffer_6

  // Notes on the sheet:
  //   Memory Data Register
endmodule

module _6_bit_Cell (
  input  Clock,
  input  Enable,
  input  R_W,
  input  [5:0] Data_In,
  input  Reset,
  output Clock_Out,
  output [5:0] Data_Out,
  output Reset_Out
);

  wire and_1_out, and_2_out, not_1_out, not_2_out;
  wire [5:0] ffd_1_q;

  and and_1 (and_1_out, Enable, ~R_W);  // AND_Gate
  and and_2 (and_2_out, Clock, Enable, R_W);
  not not_1 (not_1_out, Reset);
  FFD ffd_1 (.Clock(and_2_out), .D(Data_In[0]), .Habilitar(not_1_out), .Q(ffd_1_q[0]));  // open: nQ
  FFD ffd_2 (.Clock(and_2_out), .D(Data_In[1]), .Habilitar(not_1_out), .Q(ffd_1_q[1]));  // open: nQ
  FFD ffd_3 (.Clock(and_2_out), .D(Data_In[2]), .Habilitar(not_1_out), .Q(ffd_1_q[2]));  // open: nQ
  FFD ffd_4 (.Clock(and_2_out), .D(Data_In[3]), .Habilitar(not_1_out), .Q(ffd_1_q[3]));  // open: nQ
  FFD ffd_5 (.Clock(and_2_out), .D(Data_In[4]), .Habilitar(not_1_out), .Q(ffd_1_q[4]));  // open: nQ
  FFD ffd_6 (.Clock(and_2_out), .D(Data_In[5]), .Habilitar(not_1_out), .Q(ffd_1_q[5]));  // open: nQ
  assign Data_Out = and_1_out ? ffd_1_q : 6'bz;  // Controlled_Buffer controlled_buffer_1
  not not_2 (not_2_out, and_1_out);
  assign Data_Out = not_2_out ? {6{1'b0}} : 6'bz;  // Controlled_Buffer controlled_buffer_2

  assign Clock_Out = Clock;
  assign Reset_Out = Reset;
endmodule
