// Logisim project Memory Unit (Full Packed).circ as structural Verilog: 8 circuits, main circuit 6 bit Cell
module Neumann_s_Memory_Unit (
  input  Clock,
  input  Reset,
  input  Enable,
  input  R___W,
  input  [3:0] Adress_In,
  input  [5:0] Data_In,
  input  MAR_R_W,
  input  MDR_R_W,
  input  MAR_Enable,
  input  MDR_Enable,
  output [5:0] Data_Out
);

  wire [3:0] mar_1_adress_out;
  wire [5:0] mdr_1_ram_data_out, ram_1_data_out;

  MAR mar_1 (
    .Reset(Reset), .Adress_In(Adress_In), .R___W(MAR_R_W), .Enable(MAR_Enable),
    .Adress_Out(mar_1_adress_out), .Clock(Clock));
  RAM ram_1 (
    .Enable(Enable), .Clock(Clock), .Data_In(mdr_1_ram_data_out), .R___W(R___W),
    .Adress_In(mar_1_adress_out), .Reset(Reset), .Data_Out(ram_1_data_out));
  MDR mdr_1 (
    .Bus_Data_In(Data_In), .MDR_R___W(MDR_R_W), .Enable(MDR_Enable), .Reset(Reset), .Bus_Data_Out(Data_Out),
    .Clock(Clock), .RAM_Data_In(ram_1_data_out), .RAM_Data_Out(mdr_1_ram_data_out), .Memory_Unit_R_W(R___W));
endmodule

module RAM (
  input  Enable,
  input  [3:0] Adress_In,
  input  Clock,
  input  Reset,
  input  [5:0] Data_In,
  input  R___W,
  output [5:0] Data_Out
);

  wire n6_bit_cell_1_clock_out, n6_bit_cell_1_reset_out, n6_bit_cell_2_clock_out, n6_bit_cell_2_reset_out,
       n6_bit_cell_3_clock_out, n6_bit_cell_3_reset_out, n6_bit_cell_4_clock_out, n6_bit_cell_4_reset_out,
       n6_bit_cell_5_clock_out, n6_bit_cell_5_reset_out, n6_bit_cell_6_clock_out, n6_bit_cell_6_reset_out,
       n6_bit_cell_7_clock_out, n6_bit_cell_7_reset_out, n6_bit_cell_8_clock_out, n6_bit_cell_8_reset_out,
       n6_bit_cell_9_clock_out, n6_bit_cell_9_reset_out, n6_bit_cell_10_clock_out, n6_bit_cell_10_reset_out,
       n6_bit_cell_11_clock_out, n6_bit_cell_11_reset_out, n6_bit_cell_12_clock_out,
       n6_bit_cell_12_reset_out, n6_bit_cell_13_clock_out, n6_bit_cell_13_reset_out,
       n6_bit_cell_14_clock_out, n6_bit_cell_14_reset_out, n6_bit_cell_15_clock_out, n6_bit_cell_15_reset_out;
  wire [5:0] n6_bit_cell_1_data_out, n6_bit_cell_2_data_out, n6_bit_cell_3_data_out, n6_bit_cell_4_data_out,
       n6_bit_cell_5_data_out, n6_bit_cell_6_data_out, n6_bit_cell_7_data_out, n6_bit_cell_8_data_out,
       n6_bit_cell_9_data_out, n6_bit_cell_10_data_out, n6_bit_cell_11_data_out, n6_bit_cell_12_data_out,
       n6_bit_cell_13_data_out, n6_bit_cell_14_data_out, n6_bit_cell_15_data_out, n6_bit_cell_16_data_out;
  wire [15:0] decodificador_1_sel__line_out;

  _6_bit_Cell u_6_bit_cell_1 (
    .Enable(decodificador_1_sel__line_out[0]), .R_W(R___W), .Data_In(Data_In),
    .Data_Out(n6_bit_cell_1_data_out), .Clock(Clock), .Reset(Reset), .Reset_Out(n6_bit_cell_1_reset_out),
    .Clock_Out(n6_bit_cell_1_clock_out));
  _6_bit_Cell u_6_bit_cell_2 (
    .Enable(decodificador_1_sel__line_out[1]), .R_W(R___W), .Data_In(Data_In),
    .Data_Out(n6_bit_cell_2_data_out), .Clock(n6_bit_cell_1_clock_out), .Reset(n6_bit_cell_1_reset_out),
    .Reset_Out(n6_bit_cell_2_reset_out), .Clock_Out(n6_bit_cell_2_clock_out));
  _6_bit_Cell u_6_bit_cell_3 (
    .Enable(decodificador_1_sel__line_out[2]), .R_W(R___W), .Data_In(Data_In),
    .Data_Out(n6_bit_cell_3_data_out), .Clock(n6_bit_cell_2_clock_out), .Reset(n6_bit_cell_2_reset_out),
    .Reset_Out(n6_bit_cell_3_reset_out), .Clock_Out(n6_bit_cell_3_clock_out));
  _6_bit_Cell u_6_bit_cell_4 (
    .Enable(decodificador_1_sel__line_out[3]), .R_W(R___W), .Data_In(Data_In),
    .Data_Out(n6_bit_cell_4_data_out), .Clock(n6_bit_cell_3_clock_out), .Reset(n6_bit_cell_3_reset_out),
    .Reset_Out(n6_bit_cell_4_reset_out), .Clock_Out(n6_bit_cell_4_clock_out));
  _6_bit_Cell u_6_bit_cell_5 (
    .Enable(decodificador_1_sel__line_out[4]), .R_W(R___W), .Data_In(Data_In),
    .Data_Out(n6_bit_cell_5_data_out), .Clock(n6_bit_cell_4_clock_out), .Reset(n6_bit_cell_4_reset_out),
    .Reset_Out(n6_bit_cell_5_reset_out), .Clock_Out(n6_bit_cell_5_clock_out));
  _6_bit_Cell u_6_bit_cell_6 (
    .Enable(decodificador_1_sel__line_out[5]), .R_W(R___W), .Data_In(Data_In),
    .Data_Out(n6_bit_cell_6_data_out), .Clock(n6_bit_cell_5_clock_out), .Reset(n6_bit_cell_5_reset_out),
    .Reset_Out(n6_bit_cell_6_reset_out), .Clock_Out(n6_bit_cell_6_clock_out));
  _6_bit_Cell u_6_bit_cell_7 (
    .Enable(decodificador_1_sel__line_out[6]), .R_W(R___W), .Data_In(Data_In),
    .Data_Out(n6_bit_cell_7_data_out), .Clock(n6_bit_cell_6_clock_out), .Reset(n6_bit_cell_6_reset_out),
    .Reset_Out(n6_bit_cell_7_reset_out), .Clock_Out(n6_bit_cell_7_clock_out));
  _6_bit_Cell u_6_bit_cell_8 (
    .Enable(decodificador_1_sel__line_out[7]), .R_W(R___W), .Data_In(Data_In),
    .Data_Out(n6_bit_cell_8_data_out), .Clock(n6_bit_cell_7_clock_out), .Reset(n6_bit_cell_7_reset_out),
    .Reset_Out(n6_bit_cell_8_reset_out), .Clock_Out(n6_bit_cell_8_clock_out));
  _6_bit_Cell u_6_bit_cell_9 (
    .Enable(decodificador_1_sel__line_out[8]), .R_W(R___W), .Data_In(Data_In),
    .Data_Out(n6_bit_cell_9_data_out), .Clock(n6_bit_cell_8_clock_out), .Reset(n6_bit_cell_8_reset_out),
    .Reset_Out(n6_bit_cell_9_reset_out), .Clock_Out(n6_bit_cell_9_clock_out));
  _6_bit_Cell u_6_bit_cell_10 (
    .Enable(decodificador_1_sel__line_out[9]), .R_W(R___W), .Data_In(Data_In),
    .Data_Out(n6_bit_cell_10_data_out), .Clock(n6_bit_cell_9_clock_out), .Reset(n6_bit_cell_9_reset_out),
    .Reset_Out(n6_bit_cell_10_reset_out), .Clock_Out(n6_bit_cell_10_clock_out));
  _6_bit_Cell u_6_bit_cell_11 (
    .Enable(decodificador_1_sel__line_out[10]), .R_W(R___W), .Data_In(Data_In),
    .Data_Out(n6_bit_cell_11_data_out), .Clock(n6_bit_cell_10_clock_out), .Reset(n6_bit_cell_10_reset_out),
    .Reset_Out(n6_bit_cell_11_reset_out), .Clock_Out(n6_bit_cell_11_clock_out));
  _6_bit_Cell u_6_bit_cell_12 (
    .Enable(decodificador_1_sel__line_out[11]), .R_W(R___W), .Data_In(Data_In),
    .Data_Out(n6_bit_cell_12_data_out), .Clock(n6_bit_cell_11_clock_out), .Reset(n6_bit_cell_11_reset_out),
    .Reset_Out(n6_bit_cell_12_reset_out), .Clock_Out(n6_bit_cell_12_clock_out));
  _6_bit_Cell u_6_bit_cell_13 (
    .Enable(decodificador_1_sel__line_out[12]), .R_W(R___W), .Data_In(Data_In),
    .Data_Out(n6_bit_cell_13_data_out), .Clock(n6_bit_cell_12_clock_out), .Reset(n6_bit_cell_12_reset_out),
    .Reset_Out(n6_bit_cell_13_reset_out), .Clock_Out(n6_bit_cell_13_clock_out));
  _6_bit_Cell u_6_bit_cell_14 (
    .Enable(decodificador_1_sel__line_out[13]), .R_W(R___W), .Data_In(Data_In),
    .Data_Out(n6_bit_cell_14_data_out), .Clock(n6_bit_cell_13_clock_out), .Reset(n6_bit_cell_13_reset_out),
    .Reset_Out(n6_bit_cell_14_reset_out), .Clock_Out(n6_bit_cell_14_clock_out));
  _6_bit_Cell u_6_bit_cell_15 (
    .Enable(decodificador_1_sel__line_out[14]), .R_W(R___W), .Data_In(Data_In),
    .Data_Out(n6_bit_cell_15_data_out), .Clock(n6_bit_cell_14_clock_out), .Reset(n6_bit_cell_14_reset_out),
    .Reset_Out(n6_bit_cell_15_reset_out), .Clock_Out(n6_bit_cell_15_clock_out));
  _6_bit_Cell u_6_bit_cell_16 (
    .Enable(decodificador_1_sel__line_out[15]), .R_W(R___W), .Data_In(Data_In),
    .Data_Out(n6_bit_cell_16_data_out), .Clock(n6_bit_cell_15_clock_out), .Reset(n6_bit_cell_15_reset_out));  // open: Reset_Out, Clock_Out
  Decodificador decodificador_1 (._4_bit_In(Adress_In), .Sel__Line_Out(decodificador_1_sel__line_out), .Enable(Enable));
  _16_6_Merger u_16_6_merger_1 (
    ._0(n6_bit_cell_1_data_out), ._1(n6_bit_cell_2_data_out), ._2(n6_bit_cell_3_data_out),
    ._3(n6_bit_cell_4_data_out), ._4(n6_bit_cell_5_data_out), ._5(n6_bit_cell_6_data_out),
    ._6(n6_bit_cell_7_data_out), ._7(n6_bit_cell_8_data_out), ._8(n6_bit_cell_9_data_out),
    ._9(n6_bit_cell_10_data_out), ._10(n6_bit_cell_11_data_out), ._11(n6_bit_cell_12_data_out),
    ._12(n6_bit_cell_13_data_out), ._13(n6_bit_cell_14_data_out), ._14(n6_bit_cell_15_data_out),
    ._15(n6_bit_cell_16_data_out), .Out(Data_Out));

  // Notes on the sheet:
  //   Memory Storage
endmodule

module MAR (
  input  Clock,
  input  Reset,
  input  [3:0] Adress_In,
  input  R___W,
  input  Enable,
  output [3:0] Adress_Out
);

  _4_bit_Cell u_4_bit_cell_1 (
    .Enable(Enable), .R_W(R___W), .Data_In(Adress_In), .Data_Out(Adress_Out), .Clock(Clock), .Reset(Reset));

  // Notes on the sheet:
  //   Memory Adress Register
endmodule

module MDR (
  input  Clock,
  input  Memory_Unit_R_W,
  input  Reset,
  input  [5:0] RAM_Data_In,
  input  [5:0] Bus_Data_In,
  input  MDR_R___W,
  input  Enable,
  output [5:0] RAM_Data_Out,
  output [5:0] Bus_Data_Out
);

  wire and_1_out, not_1_out, not_2_out;
  wire [5:0] controlled_buffer_1_out, n6_bit_cell_1_data_out;

  not not_1 (not_1_out, Memory_Unit_R_W);
  assign controlled_buffer_1_out = not_1_out ? RAM_Data_In : 6'bz;  // Controlled_Buffer controlled_buffer_1
  assign controlled_buffer_1_out = Memory_Unit_R_W ? Bus_Data_In : 6'bz;  // Controlled_Buffer controlled_buffer_2
  and and_1 (and_1_out, MDR_R___W, Clock);
  _6_bit_Cell u_6_bit_cell_1 (
    .Enable(Enable), .R_W(MDR_R___W), .Data_In(controlled_buffer_1_out), .Data_Out(n6_bit_cell_1_data_out),
    .Clock(and_1_out), .Reset(Reset));  // open: Reset_Out, Clock_Out
  not not_2 (not_2_out, Memory_Unit_R_W);
  assign RAM_Data_Out = Memory_Unit_R_W ? n6_bit_cell_1_data_out : 6'bz;  // Controlled_Buffer controlled_buffer_3
  assign RAM_Data_Out = not_2_out ? {6{1'b0}} : 6'bz;  // Controlled_Buffer controlled_buffer_4
  assign Bus_Data_Out = not_2_out ? n6_bit_cell_1_data_out : 6'bz;  // Controlled_Buffer controlled_buffer_5
  assign Bus_Data_Out = Memory_Unit_R_W ? {6{1'b0}} : 6'bz;  // Controlled_Buffer controlled_buffer_6

  // Notes on the sheet:
  //   Memory Data Register
endmodule

module Decodificador (
  input  [3:0] _4_bit_In,
  input  Enable,
  output [15:0] Sel__Line_Out
);

  wire and_1_out, and_2_out, and_5_out, and_8_out, and_9_out, and_12_out, and_15_out, and_16_out, and_19_out,
       and_22_out, and_23_out, and_26_out, not_1_out, not_2_out, not_3_out, not_4_out, not_5_out;
  wire [15:0] and_4_out;

  not not_1 (not_1_out, _4_bit_In[2]);
  not not_2 (not_2_out, _4_bit_In[3]);
  and and_1 (and_1_out, not_2_out, not_1_out);
  not not_3 (not_3_out, _4_bit_In[1]);
  and and_2 (and_2_out, and_1_out, not_3_out);
  not not_4 (not_4_out, _4_bit_In[0]);
  and and_3 (and_4_out[1], and_2_out, _4_bit_In[0]);
  and and_4 (and_4_out[0], and_2_out, not_4_out);
  and and_5 (and_5_out, and_1_out, _4_bit_In[1]);
  and and_6 (and_4_out[2], and_5_out, not_4_out);
  and and_7 (and_4_out[3], and_5_out, _4_bit_In[0]);
  and and_8 (and_8_out, not_2_out, _4_bit_In[2]);
  and and_9 (and_9_out, and_8_out, not_3_out);
  and and_10 (and_4_out[5], and_9_out, _4_bit_In[0]);
  and and_11 (and_4_out[4], and_9_out, not_4_out);
  and and_12 (and_12_out, and_8_out, _4_bit_In[1]);
  and and_13 (and_4_out[6], and_12_out, not_4_out);
  and and_14 (and_4_out[7], and_12_out, _4_bit_In[0]);
  and and_15 (and_15_out, _4_bit_In[3], not_1_out);
  and and_16 (and_16_out, and_15_out, not_3_out);
  and and_17 (and_4_out[9], and_16_out, _4_bit_In[0]);
  and and_18 (and_4_out[8], and_16_out, not_4_out);
  and and_19 (and_19_out, and_15_out, _4_bit_In[1]);
  and and_20 (and_4_out[11], and_19_out, _4_bit_In[0]);
  and and_21 (and_4_out[10], and_19_out, not_4_out);
  and and_22 (and_22_out, _4_bit_In[3], _4_bit_In[2]);
  and and_23 (and_23_out, and_22_out, not_3_out);
  and and_24 (and_4_out[13], and_23_out, _4_bit_In[0]);
  and and_25 (and_4_out[12], and_23_out, not_4_out);
  and and_26 (and_26_out, and_22_out, _4_bit_In[1]);
  and and_27 (and_4_out[14], and_26_out, not_4_out);
  and and_28 (and_4_out[15], and_26_out, _4_bit_In[0]);
  assign Sel__Line_Out = Enable ? and_4_out : 16'bz;  // Controlled_Buffer controlled_buffer_1
  not not_5 (not_5_out, Enable);
  assign Sel__Line_Out = not_5_out ? {16{1'b0}} : 16'bz;  // Controlled_Buffer controlled_buffer_2

  // Notes on the sheet:
  //   4 bit Decoder
endmodule

module _16_6_Merger (
  input  [5:0] _0,
  input  [5:0] _1,
  input  [5:0] _2,
  input  [5:0] _3,
  input  [5:0] _4,
  input  [5:0] _5,
  input  [5:0] _6,
  input  [5:0] _7,
  input  [5:0] _8,
  input  [5:0] _9,
  input  [5:0] _10,
  input  [5:0] _11,
  input  [5:0] _12,
  input  [5:0] _13,
  input  [5:0] _14,
  input  [5:0] _15,
  output [5:0] Out
);

  wire [5:0] or_1_out, or_2_out, or_3_out, or_4_out, or_5_out, or_6_out, or_7_out, or_8_out, or_9_out,
       or_10_out, or_11_out, or_12_out, or_13_out, or_15_out;

  assign or_1_out = _0 | _1;  // OR_Gate or_1, 6 bits wide
  assign or_2_out = or_1_out | or_3_out;  // OR_Gate or_2, 6 bits wide
  assign or_3_out = _2 | _3;  // OR_Gate or_3, 6 bits wide
  assign or_4_out = _4 | _5;  // OR_Gate or_4, 6 bits wide
  assign or_5_out = or_4_out | or_6_out;  // OR_Gate or_5, 6 bits wide
  assign or_6_out = _6 | _7;  // OR_Gate or_6, 6 bits wide
  assign or_7_out = _8 | _9;  // OR_Gate or_7, 6 bits wide
  assign or_8_out = or_7_out | or_9_out;  // OR_Gate or_8, 6 bits wide
  assign or_9_out = _10 | _11;  // OR_Gate or_9, 6 bits wide
  assign or_10_out = _12 | _13;  // OR_Gate or_10, 6 bits wide
  assign or_11_out = or_10_out | or_12_out;  // OR_Gate or_11, 6 bits wide
  assign or_12_out = _14 | _15;  // OR_Gate or_12, 6 bits wide
  assign or_13_out = or_2_out | or_5_out;  // OR_Gate or_13, 6 bits wide
  assign Out = or_13_out | or_15_out;  // OR_Gate or_14, 6 bits wide
  assign or_15_out = or_8_out | or_11_out;  // OR_Gate or_15, 6 bits wide
endmodule

module _6_bit_Cell (
  input  Clock,
  input  Enable,
  input  R_W,
  input  [5:0] Data_In,
  input  Reset,
  output Clock_Out,
  output [5:0] Data_Out,
  output Reset_Out
);

  wire and_1_out, and_2_out, not_1_out, not_2_out;
  wire [5:0] ffd_1_q;

  and and_1 (and_1_out, Enable, ~R_W);  // AND_Gate
  and and_2 (and_2_out, Clock, Enable, R_W);
  not not_1 (not_1_out, Reset);
  FFD ffd_1 (.Clock(and_2_out), .D(Data_In[0]), .Habilitar(not_1_out), .Q(ffd_1_q[0]));  // open: nQ
  FFD ffd_2 (.Clock(and_2_out), .D(Data_In[1]), .Habilitar(not_1_out), .Q(ffd_1_q[1]));  // open: nQ
  FFD ffd_3 (.Clock(and_2_out), .D(Data_In[2]), .Habilitar(not_1_out), .Q(ffd_1_q[2]));  // open: nQ
  FFD ffd_4 (.Clock(and_2_out), .D(Data_In[3]), .Habilitar(not_1_out), .Q(ffd_1_q[3]));  // open: nQ
  FFD ffd_5 (.Clock(and_2_out), .D(Data_In[4]), .Habilitar(not_1_out), .Q(ffd_1_q[4]));  // open: nQ
  FFD ffd_6 (.Clock(and_2_out), .D(Data_In[5]), .Habilitar(not_1_out), .Q(ffd_1_q[5]));  // open: nQ
  assign Data_Out = and_1_out ? ffd_1_q : 6'bz;  // Controlled_Buffer controlled_buffer_1
  not not_2 (not_2_out, and_1_out);
  assign Data_Out = not_2_out ? {6{1'b0}} : 6'bz;  // Controlled_Buffer controlled_buffer_2

  assign Clock_Out = Clock;
  assign Reset_Out = Reset;
endmodule

module _4_bit_Cell (
  input  Clock,
  input  Enable,
  input  R_W,
  input  [3:0] Data_In,
  input  Reset,
  output [3:0] Data_Out
);

  wire and_1_out, and_2_out, not_1_out, not_2_out;
  wire [3:0] ffd_1_q;

  and and_1 (and_1_out, Enable, ~R_W);  // AND_Gate
  and and_2 (and_2_out, Clock, Enable, R_W);
  not not_1 (not_1_out, Reset);
  FFD ffd_1 (.Clock(and_2_out), .D(Data_In[0]), .Habilitar(not_1_out), .Q(ffd_1_q[0]));  // open: nQ
  FFD ffd_2 (.Clock(and_2_out), .D(Data_In[1]), .Habilitar(not_1_out), .Q(ffd_1_q[1]));  // open: nQ
  FFD ffd_3 (.Clock(and_2_out), .D(Data_In[2]), .Habilitar(not_1_out), .Q(ffd_1_q[2]));  // open: nQ
  FFD ffd_4 (.Clock(and_2_out), .D(Data_In[3]), .Habilitar(not_1_out), .Q(ffd_1_q[3]));  // open: nQ
  not not_2 (not_2_out, and_1_out);
  assign Data_Out = and_1_out ? ffd_1_q : 4'bz;  // Controlled_Buffer controlled_buffer_1
  assign Data_Out = not_2_out ? 4'b0000 : 4'bz;  // Controlled_Buffer controlled_buffer_2
endmodule
