// Logisim project TEST.circ as structural Verilog: 4 circuits, main circuit Neumann's Memory Unit
module RAM_TEST (
  input  Clock,
  input  Reset,
  input  Enable,
  input  [5:0] Data,
  input  [3:0] Address,
  input  R_W,
  output [5:0] Data_2
);

  RAM ram_1 (
    .Enable(Enable), .Clock(Clock), .Data_In(Data), .R___W(R_W), .Adress_In(Address), .Reset(Reset),
    .Data_Out(Data_2));

  // Notes on the sheet:
  //   Random Access Memory
endmodule

module MAR_TEST (
  input  Clock,
  input  Reset,
  input  [3:0] Address,
  input  R_W,
  input  Enable,
  output [3:0] Data
);

  MAR mar_1 (.Reset(Reset), .Adress_In(Address), .R___W(R_W), .Enable(Enable), .Adress_Out(Data), .Clock(Clock));

  // Notes on the sheet:
  //   Memory Address Register
endmodule

module MDR_TEST (
  input  Clock,
  input  Reset,
  input  [5:0] Bus_Data,
  input  [5:0] RAM_Data,
  input  R_W,
  input  RAM_R_W,
  input  Enable,
  output [5:0] Bus_Data_2,
  output [5:0] RAM_Data_2
);

  MDR mdr_1 (
    .Bus_Data_In(Bus_Data), .MDR_R___W(R_W), .Enable(Enable), .Reset(Reset), .Bus_Data_Out(Bus_Data_2),
    .Clock(Clock), .RAM_Data_In(RAM_Data), .RAM_Data_Out(RAM_Data_2), .Memory_Unit_R_W(RAM_R_W));

  // Notes on the sheet:
  //   Memory Data Register
endmodule

module Neumann_s_Memory_Unit (
  input  Clock,
  input  Reset,
  input  Enable,
  input  R___W,
  input  [3:0] Adress_In,
  input  [5:0] Data_In,
  input  MAR_R_W,
  input  MDR_R_W,
  input  MAR_Enable,
  input  MDR_Enable,
  output [5:0] Data_Out
);

  wire [3:0] mar_1_adress_out;
  wire [5:0] mdr_1_ram_data_out, ram_1_data_out;

  MAR mar_1 (
    .Reset(Reset), .Adress_In(Adress_In), .R___W(MAR_R_W), .Enable(MAR_Enable),
    .Adress_Out(mar_1_adress_out), .Clock(Clock));
  RAM ram_1 (
    .Enable(Enable), .Clock(Clock), .Data_In(mdr_1_ram_data_out), .R___W(R___W),
    .Adress_In(mar_1_adress_out), .Reset(Reset), .Data_Out(ram_1_data_out));
  MDR mdr_1 (
    .Bus_Data_In(Data_In), .MDR_R___W(MDR_R_W), .Enable(MDR_Enable), .Reset(Reset), .Bus_Data_Out(Data_Out),
    .Clock(Clock), .RAM_Data_In(ram_1_data_out), .RAM_Data_Out(mdr_1_ram_data_out), .Memory_Unit_R_W(R___W));
endmodule
