// Logisim project Almacenamiento Universal.circ as structural Verilog: 2 circuits, main circuit Universal Storage
module Universal_Storage (
  input  Reset,
  input  Enable,
  input  R___W,
  input  Mode,
  input  [5:0] In,
  output [5:0] Out
);

  wire and_1_out, Clock_out, controlled_buffer_1_out, ffd_1_q, ffd_2_q, ffd_3_q, ffd_4_q, ffd_5_q, ffd_6_q,
       nextbit_1_next_out, nextbit_1_self_out, nextbit_2_next_out, nextbit_2_self_out, nextbit_3_next_out,
       nextbit_3_self_out, nextbit_4_next_out, nextbit_4_self_out, nextbit_5_next_out, nextbit_5_self_out,
       nextbit_6_next_out, nextbit_6_parallel_out, nextbit_6_self_out, not_1_out, not_2_out, not_3_out,
       not_4_out;
  wire [5:0] controlled_buffer_3_out;

  Clock Clock (.out(Clock_out));
  not not_1 (not_1_out, Reset);
  and and_1 (and_1_out, Clock_out, Enable);
  assign controlled_buffer_1_out = R___W ? In[0] : 1'bz;  // Controlled_Buffer controlled_buffer_1
  not not_2 (not_2_out, R___W);
  assign controlled_buffer_1_out = not_2_out ? nextbit_6_next_out : 1'bz;  // Controlled_Buffer controlled_buffer_2
  FFD ffd_1 (.Clock(and_1_out), .D(nextbit_1_self_out), .Habilitar(not_1_out), .Q(ffd_1_q));  // open: nQ
  nextBit nextbit_1 (
    .Previous_In(controlled_buffer_1_out), .Self_In(ffd_1_q), .Parallel_In(In[5]),
    .Self_Out(nextbit_1_self_out), .Next_Out(nextbit_1_next_out), .Parallel_Out(controlled_buffer_3_out[5]),
    .R_W(R___W), .Mode(Mode));
  FFD ffd_2 (.Clock(and_1_out), .D(nextbit_2_self_out), .Habilitar(not_1_out), .Q(ffd_2_q));  // open: nQ
  nextBit nextbit_2 (
    .Previous_In(nextbit_1_next_out), .Self_In(ffd_2_q), .Parallel_In(In[4]), .Self_Out(nextbit_2_self_out),
    .Next_Out(nextbit_2_next_out), .Parallel_Out(controlled_buffer_3_out[4]), .R_W(R___W), .Mode(Mode));
  FFD ffd_3 (.Clock(and_1_out), .D(nextbit_4_self_out), .Habilitar(not_1_out), .Q(ffd_3_q));  // open: nQ
  FFD ffd_4 (.Clock(and_1_out), .D(nextbit_3_self_out), .Habilitar(not_1_out), .Q(ffd_4_q));  // open: nQ
  nextBit nextbit_3 (
    .Previous_In(nextbit_4_next_out), .Self_In(ffd_4_q), .Parallel_In(In[2]), .Self_Out(nextbit_3_self_out),
    .Next_Out(nextbit_3_next_out), .Parallel_Out(controlled_buffer_3_out[2]), .R_W(R___W), .Mode(Mode));
  nextBit nextbit_4 (
    .Previous_In(nextbit_2_next_out), .Self_In(ffd_3_q), .Parallel_In(In[3]), .Self_Out(nextbit_4_self_out),
    .Next_Out(nextbit_4_next_out), .Parallel_Out(controlled_buffer_3_out[3]), .R_W(R___W), .Mode(Mode));
  FFD ffd_5 (.Clock(and_1_out), .D(nextbit_5_self_out), .Habilitar(not_1_out), .Q(ffd_5_q));  // open: nQ
  nextBit nextbit_5 (
    .Previous_In(nextbit_3_next_out), .Self_In(ffd_5_q), .Parallel_In(In[1]), .Self_Out(nextbit_5_self_out),
    .Next_Out(nextbit_5_next_out), .Parallel_Out(controlled_buffer_3_out[1]), .R_W(R___W), .Mode(Mode));
  FFD ffd_6 (.Clock(and_1_out), .D(nextbit_6_self_out), .Habilitar(not_1_out), .Q(ffd_6_q));  // open: nQ
  nextBit nextbit_6 (
    .Previous_In(nextbit_5_next_out), .Self_In(ffd_6_q), .Parallel_In(In[0]), .Self_Out(nextbit_6_self_out),
    .Next_Out(nextbit_6_next_out), .Parallel_Out(nextbit_6_parallel_out), .R_W(R___W), .Mode(Mode));
  assign controlled_buffer_3_out[0] = Mode ? nextbit_6_parallel_out : 1'bz;  // Controlled_Buffer controlled_buffer_3
  not not_3 (not_3_out, Mode);
  assign controlled_buffer_3_out[0] = not_3_out ? nextbit_6_next_out : 1'bz;  // Controlled_Buffer controlled_buffer_4
  assign Out = not_4_out ? {6{1'b0}} : 6'bz;  // Controlled_Buffer controlled_buffer_5
  not not_4 (not_4_out, Enable);
  assign Out = Enable ? controlled_buffer_3_out : 6'bz;  // Controlled_Buffer controlled_buffer_6

  // Notes on the sheet:
  //   Activación
  //   Modo
  //   Entrada
  //   Salida
endmodule

module nextBit (
  input  Previous_In,
  input  Self_In,
  input  Parallel_In,
  input  R_W,
  input  Mode,
  output Self_Out,
  output Next_Out,
  output Parallel_Out
);

  wire and_1_out, and_2_out, not_1_out, not_2_out, xnor_1_out;

  assign Self_Out = xnor_1_out ? Previous_In : 1'bz;  // Controlled_Buffer controlled_buffer_1
  assign Self_Out = and_1_out ? Self_In : 1'bz;  // Controlled_Buffer controlled_buffer_2
  xnor xnor_1 (xnor_1_out, R_W, Mode);
  and and_1 (and_1_out, ~R_W, Mode);  // AND_Gate
  assign Self_Out = and_2_out ? Parallel_In : 1'bz;  // Controlled_Buffer controlled_buffer_3
  assign Next_Out = xnor_1_out ? Self_In : 1'bz;  // Controlled_Buffer controlled_buffer_4
  assign Next_Out = not_1_out ? 1'b0 : 1'bz;  // Controlled_Buffer controlled_buffer_5
  not not_1 (not_1_out, xnor_1_out);
  assign Parallel_Out = and_1_out ? Self_In : 1'bz;  // Controlled_Buffer controlled_buffer_6
  assign Parallel_Out = not_2_out ? 1'b0 : 1'bz;  // Controlled_Buffer controlled_buffer_7
  not not_2 (not_2_out, and_1_out);
  and and_2 (and_2_out, R_W, ~Mode);  // AND_Gate
endmodule
