// Logisim project Parallel in-Serial out.circ as structural Verilog: 1 circuit, main circuit Parallel-In/Serial-Out
module Parallel_In_Serial_Out (
  input  Reset,
  input  Modo,
  input  [5:0] Parallel_In,
  input  R___W,
  input  Habilitar,
  output Serial_Out
);

  wire and_1_out, and_2_out, Clock_out, controlled_buffer_1_out, controlled_buffer_2_out,
       controlled_buffer_4_out, controlled_buffer_6_out, controlled_buffer_8_out, controlled_buffer_10_out,
       controlled_buffer_12_out, ffd_1_q, ffd_2_q, ffd_3_q, ffd_4_q, ffd_5_q, not_1_out, not_2_out,
       not_3_out, not_4_out, not_5_out, not_6_out, not_7_out, not_8_out;

  Clock Clock (.out(Clock_out));
  not not_1 (not_1_out, Reset);
  not not_2 (not_2_out, Modo);
  and and_1 (and_1_out, Clock_out, Habilitar);
  and and_2 (and_2_out, not_1_out, Habilitar);
  assign controlled_buffer_1_out = not_2_out ? controlled_buffer_2_out : 1'bz;  // Controlled_Buffer controlled_buffer_1
  assign controlled_buffer_2_out = not_4_out ? Serial_Out : 1'bz;  // Controlled_Buffer controlled_buffer_2
  assign controlled_buffer_2_out = R___W ? Parallel_In[5] : 1'bz;  // Controlled_Buffer controlled_buffer_3
  FFD ffd_1 (.Clock(and_1_out), .D(controlled_buffer_1_out), .Habilitar(and_2_out), .Q(ffd_1_q));  // open: nQ
  assign controlled_buffer_4_out = not_3_out ? ffd_1_q : 1'bz;  // Controlled_Buffer controlled_buffer_4
  assign controlled_buffer_4_out = R___W ? Parallel_In[4] : 1'bz;  // Controlled_Buffer controlled_buffer_5
  not not_3 (not_3_out, R___W);
  not not_4 (not_4_out, R___W);
  FFD ffd_2 (.Clock(and_1_out), .D(controlled_buffer_4_out), .Habilitar(and_2_out), .Q(ffd_2_q));  // open: nQ
  assign controlled_buffer_6_out = not_5_out ? ffd_2_q : 1'bz;  // Controlled_Buffer controlled_buffer_6
  assign controlled_buffer_6_out = R___W ? Parallel_In[3] : 1'bz;  // Controlled_Buffer controlled_buffer_7
  not not_5 (not_5_out, R___W);
  FFD ffd_3 (.Clock(and_1_out), .D(controlled_buffer_8_out), .Habilitar(and_2_out), .Q(ffd_3_q));  // open: nQ
  FFD ffd_4 (.Clock(and_1_out), .D(controlled_buffer_6_out), .Habilitar(and_2_out), .Q(ffd_4_q));  // open: nQ
  assign controlled_buffer_8_out = not_6_out ? ffd_4_q : 1'bz;  // Controlled_Buffer controlled_buffer_8
  assign controlled_buffer_8_out = R___W ? Parallel_In[2] : 1'bz;  // Controlled_Buffer controlled_buffer_9
  not not_6 (not_6_out, R___W);
  FFD ffd_5 (.Clock(and_1_out), .D(controlled_buffer_10_out), .Habilitar(and_2_out), .Q(ffd_5_q));  // open: nQ
  assign controlled_buffer_10_out = not_7_out ? ffd_3_q : 1'bz;  // Controlled_Buffer controlled_buffer_10
  assign controlled_buffer_10_out = R___W ? Parallel_In[1] : 1'bz;  // Controlled_Buffer controlled_buffer_11
  not not_7 (not_7_out, R___W);
  FFD ffd_6 (.Clock(and_1_out), .D(controlled_buffer_12_out), .Habilitar(and_2_out), .Q(Serial_Out));  // open: nQ
  assign controlled_buffer_12_out = not_8_out ? ffd_5_q : 1'bz;  // Controlled_Buffer controlled_buffer_12
  assign controlled_buffer_12_out = R___W ? Parallel_In[0] : 1'bz;  // Controlled_Buffer controlled_buffer_13
  not not_8 (not_8_out, R___W);
endmodule
