// Logisim project Serial in-Parallel out.circ as structural Verilog: 1 circuit, main circuit Serial-In/Parallel-Out
module Serial_In_Parallel_Out (
  input  Serial_Input,
  input  Reset,
  input  R___W,
  input  Habilitar,
  output [5:0] Parallel_Output
);

  wire and_1_out, Clk_out, controlled_buffer_1_out, controlled_buffer_3_out, controlled_buffer_4_out,
       controlled_buffer_7_out, controlled_buffer_9_out, controlled_buffer_11_out, not_1_out, not_2_out,
       not_3_out, not_4_out, not_5_out, not_6_out, not_7_out, not_8_out, or_1_out;
  wire [5:0] d_ff_6_q;

  Clock Clk (.out(Clk_out));
  assign controlled_buffer_1_out = R___W ? Serial_Input : 1'bz;  // Controlled_Buffer controlled_buffer_1
  and and_1 (and_1_out, Clk_out, Habilitar);
  D_Flip_Flop d_ff_1 (
    .clk(and_1_out), .D(controlled_buffer_1_out), .Q(d_ff_6_q[5]), .reset(Reset));  // open: Qn, preset, en
  assign controlled_buffer_1_out = not_1_out ? d_ff_6_q[5] : 1'bz;  // Controlled_Buffer controlled_buffer_2
  not not_1 (not_1_out, R___W);
  or or_1 (or_1_out, R___W, not_2_out);
  not not_2 (not_2_out, Habilitar);
  D_Flip_Flop d_ff_2 (
    .clk(and_1_out), .D(controlled_buffer_3_out), .Q(d_ff_6_q[4]), .reset(Reset));  // open: Qn, preset, en
  assign controlled_buffer_3_out = not_3_out ? d_ff_6_q[4] : 1'bz;  // Controlled_Buffer controlled_buffer_3
  not not_3 (not_3_out, R___W);
  assign controlled_buffer_4_out = R___W ? d_ff_6_q[4] : 1'bz;  // Controlled_Buffer controlled_buffer_4
  assign controlled_buffer_3_out = R___W ? d_ff_6_q[5] : 1'bz;  // Controlled_Buffer controlled_buffer_5
  D_Flip_Flop d_ff_3 (
    .clk(and_1_out), .D(controlled_buffer_4_out), .Q(d_ff_6_q[3]), .reset(Reset));  // open: Qn, preset, en
  assign controlled_buffer_4_out = not_4_out ? d_ff_6_q[3] : 1'bz;  // Controlled_Buffer controlled_buffer_6
  assign controlled_buffer_7_out = R___W ? d_ff_6_q[3] : 1'bz;  // Controlled_Buffer controlled_buffer_7
  not not_4 (not_4_out, R___W);
  D_Flip_Flop d_ff_4 (
    .clk(and_1_out), .D(controlled_buffer_7_out), .Q(d_ff_6_q[2]), .reset(Reset));  // open: Qn, preset, en
  assign controlled_buffer_7_out = not_5_out ? d_ff_6_q[2] : 1'bz;  // Controlled_Buffer controlled_buffer_8
  assign controlled_buffer_9_out = not_7_out ? d_ff_6_q[1] : 1'bz;  // Controlled_Buffer controlled_buffer_9
  assign controlled_buffer_9_out = R___W ? d_ff_6_q[2] : 1'bz;  // Controlled_Buffer controlled_buffer_10
  not not_5 (not_5_out, R___W);
  D_Flip_Flop d_ff_5 (
    .clk(and_1_out), .D(controlled_buffer_9_out), .Q(d_ff_6_q[1]), .reset(Reset));  // open: Qn, preset, en
  assign controlled_buffer_11_out = not_6_out ? d_ff_6_q[0] : 1'bz;  // Controlled_Buffer controlled_buffer_11
  assign controlled_buffer_11_out = R___W ? d_ff_6_q[1] : 1'bz;  // Controlled_Buffer controlled_buffer_12
  not not_6 (not_6_out, R___W);
  not not_7 (not_7_out, R___W);
  not not_8 (not_8_out, or_1_out);
  assign Parallel_Output = or_1_out ? {6{1'b0}} : 6'bz;  // Controlled_Buffer controlled_buffer_13
  D_Flip_Flop d_ff_6 (
    .clk(and_1_out), .D(controlled_buffer_11_out), .Q(d_ff_6_q[0]), .reset(Reset));  // open: Qn, preset, en
  assign Parallel_Output = not_8_out ? d_ff_6_q : 6'bz;  // Controlled_Buffer controlled_buffer_14
endmodule
