// Logisim project Investor.circ as structural Verilog: 1 circuit, main circuit main
module main (
  input  [5:0] Data,
  input  Enabling,
  output [5:0] Exit
);

  wire not_2_out;
  wire [5:0] not_1_out;

  assign not_1_out = ~Data;  // NOT_Gate not_1, 6 bits wide
  assign Exit = Enabling ? not_1_out : 6'bz;  // Controlled_Buffer controlled_buffer_1
  assign Exit = not_2_out ? {6{1'b0}} : 6'bz;  // Controlled_Buffer controlled_buffer_2
  not not_2 (not_2_out, Enabling);
endmodule
