// Logisim project Multiplexor3.circ as structural Verilog: 1 circuit, main circuit main
module main (
  input  [5:0] Data,
  input  [1:0] Function,
  output [5:0] Exit
);

  wire and_1_out, and_2_out, and_3_out, and_4_out;
  wire [5:0] main_1_exit, main_2_out_3, main_3_out_3, select_6_1_respuesta;

  and and_1 (and_1_out, ~Function[0], ~Function[1]);  // AND_Gate
  and and_2 (and_2_out, Function[0], ~Function[1]);  // AND_Gate
  and and_3 (and_3_out, ~Function[0], Function[1]);  // AND_Gate
  and and_4 (and_4_out, Function[0], Function[1]);
  Select_6 select_6_1 (.A({6{1'b0}}), .B(Data), .Habilitador(and_1_out), .Respuesta(select_6_1_respuesta));
  Investor_main main_1 (.Data(Data), .Enabling(and_2_out), .Exit(main_1_exit));
  SHL_0_main main_2 (.in_1(Data), .in_2(and_3_out), .out_3(main_2_out_3));
  SHRA_main main_3 (.in_1(Data), .Habilitador(and_4_out), .out_3(main_3_out_3));
  assign Exit = select_6_1_respuesta | main_1_exit | main_2_out_3 | main_3_out_3;  // OR_Gate or_1, 6 bits wide
endmodule
