// Logisim project SHRA.circ as structural Verilog: 1 circuit, main circuit main
module main (
  input  [5:0] in_1,
  input  Habilitador,
  output [5:0] out_3
);

  and and_1 (out_3[0], in_1[1], Habilitador);
  and and_2 (out_3[1], in_1[2], Habilitador);
  and and_3 (out_3[2], in_1[3], Habilitador);
  and and_4 (out_3[3], in_1[4], Habilitador);
  and and_5 (out_3[5], in_1[5], Habilitador);

  assign out_3[4] = out_3[5];

  // Notes on the sheet:
  //   Palabra
  //   Resultado
endmodule
