// Logisim project Test.circ as structural Verilog: 1 circuit, main circuit main
module main (
  input  R_W,
  input  [1:0] Function,
  input  Reset,
  input  [5:0] Data,
  input  Enabiling,
  output [5:0] Exit
);

  wire Clock_out;

  Clock Clock (.out(Clock_out));
  Work_register_main main_1 (
    .R___W(R_W), .Function(Function), .Reset(Reset), .Data(Data), .Enabling(Enabiling), .Exit(Exit),
    .Clock(Clock_out));
endmodule
