// Logisim project Work_register.circ as structural Verilog: 1 circuit, main circuit main
module main (
  input  Clock,
  input  R___W,
  input  [1:0] Function,
  input  Reset,
  input  [5:0] Data,
  input  Enabling,
  output [5:0] Exit
);

  wire and_1_out, and_2_out, not_1_out, not_2_out;
  wire [5:0] ffd_5_q, main_1_exit;

  and and_1 (and_1_out, Clock, R___W, Enabling);
  and and_2 (and_2_out, Enabling, Reset);
  FFD ffd_1 (.Clock(and_1_out), .D(Data[5]), .Habilitar(not_1_out), .Q(ffd_5_q[5]));  // open: nQ
  not not_1 (not_1_out, and_2_out);
  FFD ffd_2 (.Clock(and_1_out), .D(Data[4]), .Habilitar(not_1_out), .Q(ffd_5_q[4]));  // open: nQ
  FFD ffd_3 (.Clock(and_1_out), .D(Data[3]), .Habilitar(not_1_out), .Q(ffd_5_q[3]));  // open: nQ
  Multiplexor3_main main_1 (.Data(ffd_5_q), .Function(Function), .Exit(main_1_exit));
  FFD ffd_4 (.Clock(and_1_out), .D(Data[2]), .Habilitar(not_1_out), .Q(ffd_5_q[2]));  // open: nQ
  FFD ffd_5 (.Clock(and_1_out), .D(Data[0]), .Habilitar(not_1_out), .Q(ffd_5_q[0]));  // open: nQ
  FFD ffd_6 (.Clock(and_1_out), .D(Data[1]), .Habilitar(not_1_out), .Q(ffd_5_q[1]));  // open: nQ
  assign Exit = Enabling ? main_1_exit : 6'bz;  // Controlled_Buffer controlled_buffer_1
  assign Exit = not_2_out ? {6{1'b0}} : 6'bz;  // Controlled_Buffer controlled_buffer_2
  not not_2 (not_2_out, Enabling);
endmodule
